// Logisim project Marcos_Arquitetura.circ as structural Verilog: 9 circuits, main circuit main
module main (
  input  [3:0] A,
  input  [3:0] B,
  input  [2:0] in_3,
  output Overflow,
  output out_5,
  output [3:0] S
);

  wire decoder_1_d0, decoder_1_d1, decoder_1_d2, decoder_1_d3, decoder_1_d4;
  wire [3:0] add_4_1_out_4, rot_dir_1_abcd_2, rot_esq_1_abcd_2, sub_4_1_out_4;

  Decoder decoder_1 (
    .in_1(in_3), .D0(decoder_1_d0), .D1(decoder_1_d1), .D2(decoder_1_d2), .D3(decoder_1_d3), .D4(decoder_1_d4));  // open: D5, D6, D7
  // Probe on A
  // Probe on add_4_1_out_4
  Buffer buffer_1 (.E(B), .C(decoder_1_d0), .S(S));
  // Probe on A
  // Probe on B
  ADD_4 add_4_1 (.A(A), .Overflow(Overflow), .B(B), .out_4(add_4_1_out_4));
  Buffer buffer_2 (.E(add_4_1_out_4), .C(decoder_1_d1), .S(S));
  // Probe on B
  SUB_4 sub_4_1 (.A(A), .Overflow(out_5), .B(B), .out_4(sub_4_1_out_4));
  // Probe on sub_4_1_out_4
  Buffer buffer_3 (.E(sub_4_1_out_4), .C(decoder_1_d2), .S(S));
  Rot_Esq rot_esq_1 (.abcd(A), .xy(B[1:0]), .ABCD_2(rot_esq_1_abcd_2));
  Rot_Dir rot_dir_1 (.abcd(A), .xy(B[1:0]), .ABCD_2(rot_dir_1_abcd_2));
  Buffer buffer_4 (.E(rot_dir_1_abcd_2), .C(decoder_1_d3), .S(S));
  Buffer buffer_5 (.E(rot_esq_1_abcd_2), .C(decoder_1_d4), .S(S));
endmodule

module ADD_1 (
  input  A,
  input  B,
  input  C,
  output SOMA,
  output VAI_1
);

  wire and_1_out, and_2_out, or_1_out, xor_1_out;

  xor xor_1 (xor_1_out, C, B);
  or or_1 (or_1_out, B, C);
  and and_1 (and_1_out, B, C);
  xor xor_2 (SOMA, xor_1_out, A);
  and and_2 (and_2_out, or_1_out, A);
  or or_2 (VAI_1, and_2_out, and_1_out);
endmodule

module ADD_4 (
  input  [3:0] B,
  input  [3:0] A,
  output Overflow,
  output [3:0] out_4
);

  wire add_1_2_vai_1, add_1_3_vai_1, add_1_4_vai_1;

  // Probe on A
  ADD_1 add_1_1 (.VAI_1(Overflow), .A(A[3]), .B(B[3]), .C(add_1_2_vai_1), .SOMA(out_4[3]));
  ADD_1 add_1_2 (.VAI_1(add_1_2_vai_1), .A(A[2]), .B(B[2]), .C(add_1_3_vai_1), .SOMA(out_4[2]));
  ADD_1 add_1_3 (.VAI_1(add_1_3_vai_1), .A(A[1]), .B(B[1]), .C(add_1_4_vai_1), .SOMA(out_4[1]));
  // Probe on out_4
  ADD_1 add_1_4 (.VAI_1(add_1_4_vai_1), .A(A[0]), .B(B[0]), .C(1'b0), .SOMA(out_4[0]));
  // Probe on B
endmodule

module SUB_1 (
  input  A,
  input  B,
  input  C,
  output SOMA,
  output VAI_1
);

  wire and_1_out, and_2_out, or_1_out, xor_1_out;

  xor xor_1 (xor_1_out, C, B);
  or or_1 (or_1_out, B, C);
  and and_1 (and_1_out, B, C);
  xor xor_2 (SOMA, xor_1_out, A);
  and and_2 (and_2_out, or_1_out, ~A);  // AND_Gate
  or or_2 (VAI_1, and_2_out, and_1_out);
endmodule

module SUB_4 (
  input  [3:0] B,
  input  [3:0] A,
  output Overflow,
  output [3:0] out_4
);

  wire sub_1_2_vai_1, sub_1_3_vai_1, sub_1_4_vai_1;

  // Probe on A
  SUB_1 sub_1_1 (.VAI_1(Overflow), .A(A[3]), .B(B[3]), .C(sub_1_2_vai_1), .SOMA(out_4[3]));
  SUB_1 sub_1_2 (.VAI_1(sub_1_2_vai_1), .A(A[2]), .B(B[2]), .C(sub_1_3_vai_1), .SOMA(out_4[2]));
  SUB_1 sub_1_3 (.VAI_1(sub_1_3_vai_1), .A(A[1]), .B(B[1]), .C(sub_1_4_vai_1), .SOMA(out_4[1]));
  // Probe on out_4
  // Probe on B
  SUB_1 sub_1_4 (.VAI_1(sub_1_4_vai_1), .A(A[0]), .B(B[0]), .C(1'b0), .SOMA(out_4[0]));
endmodule

module Rot_Esq (
  input  [3:0] abcd,
  input  [1:0] xy,
  output [3:0] ABCD_2
);

  wire and_1_out, and_2_out, and_3_out, and_4_out, and_5_out, and_6_out, and_7_out, and_8_out, and_9_out;

  and and_1 (and_1_out, abcd[3], ~xy[1], ~xy[0]);  // AND_Gate
  and and_2 (and_2_out, abcd[2], ~xy[1], xy[0]);  // AND_Gate
  and and_3 (and_3_out, abcd[1], xy[1], ~xy[0]);  // AND_Gate
  and and_4 (and_4_out, abcd[0], xy[1], xy[0]);
  and and_5 (and_5_out, abcd[2], ~xy[1], ~xy[0]);  // AND_Gate
  and and_6 (and_6_out, abcd[1], ~xy[1], xy[0]);  // AND_Gate
  and and_7 (and_7_out, abcd[0], xy[1], ~xy[0]);  // AND_Gate
  and and_8 (and_8_out, abcd[1], ~xy[1], ~xy[0]);  // AND_Gate
  and and_9 (and_9_out, abcd[0], ~xy[1], xy[0]);  // AND_Gate
  and and_10 (ABCD_2[0], abcd[0], ~xy[1], ~xy[0]);  // AND_Gate
  or or_1 (ABCD_2[3], and_1_out, and_2_out, and_3_out, and_4_out);
  or or_2 (ABCD_2[2], and_5_out, and_6_out, and_7_out);
  or or_3 (ABCD_2[1], and_8_out, and_9_out);
endmodule

module Rot_Dir (
  input  [3:0] abcd,
  input  [1:0] xy,
  output [3:0] ABCD_2
);

  wire and_1_out, and_2_out, and_3_out, and_4_out, and_5_out, and_6_out, and_7_out, and_8_out, and_9_out;

  and and_1 (and_1_out, abcd[0], ~xy[1], ~xy[0]);  // AND_Gate
  and and_2 (and_2_out, abcd[1], ~xy[1], xy[0]);  // AND_Gate
  and and_3 (and_3_out, abcd[2], xy[1], ~xy[0]);  // AND_Gate
  and and_4 (and_4_out, abcd[3], xy[1], xy[0]);
  and and_5 (and_5_out, abcd[1], ~xy[1], ~xy[0]);  // AND_Gate
  and and_6 (and_6_out, abcd[2], ~xy[1], xy[0]);  // AND_Gate
  and and_7 (and_7_out, abcd[3], xy[1], ~xy[0]);  // AND_Gate
  and and_8 (and_8_out, abcd[2], ~xy[1], ~xy[0]);  // AND_Gate
  and and_9 (and_9_out, abcd[3], ~xy[1], xy[0]);  // AND_Gate
  and and_10 (ABCD_2[3], abcd[3], ~xy[1], ~xy[0]);  // AND_Gate
  or or_1 (ABCD_2[0], and_1_out, and_2_out, and_3_out, and_4_out);
  or or_2 (ABCD_2[1], and_5_out, and_6_out, and_7_out);
  or or_3 (ABCD_2[2], and_8_out, and_9_out);
endmodule

module Decoder (
  input  [2:0] in_1,
  output D0,
  output D1,
  output D2,
  output D3,
  output D4,
  output D5,
  output D6,
  output D7
);

  wire not_1_out, not_2_out, not_3_out, not_4_out, not_5_out, not_6_out, not_7_out, not_8_out, not_9_out,
       not_10_out, not_11_out, not_12_out;

  not not_1 (not_1_out, in_1[2]);
  not not_2 (not_2_out, in_1[1]);
  not not_3 (not_3_out, in_1[0]);
  not not_4 (not_4_out, in_1[2]);
  not not_5 (not_5_out, in_1[1]);
  not not_6 (not_6_out, in_1[2]);
  not not_7 (not_7_out, in_1[0]);
  not not_8 (not_8_out, in_1[2]);
  not not_9 (not_9_out, in_1[1]);
  not not_10 (not_10_out, in_1[0]);
  not not_11 (not_11_out, in_1[1]);
  not not_12 (not_12_out, in_1[0]);
  and and_1 (D7, in_1[2], in_1[1], in_1[0]);
  and and_2 (D0, not_1_out, not_2_out, not_3_out);
  and and_3 (D1, not_4_out, not_5_out, in_1[0]);
  and and_4 (D2, not_6_out, in_1[1], not_7_out);
  and and_5 (D3, not_8_out, in_1[1], in_1[0]);
  and and_6 (D4, in_1[2], not_9_out, not_10_out);
  and and_7 (D5, in_1[2], not_11_out, in_1[0]);
  and and_8 (D6, in_1[2], in_1[1], not_12_out);
endmodule

module Buffer (
  input  [3:0] E,
  input  C,
  output [3:0] S
);

  assign S[3] = C ? E[3] : 1'bz;  // Controlled_Buffer controlled_buffer_1
  assign S[2] = C ? E[2] : 1'bz;  // Controlled_Buffer controlled_buffer_2
  assign S[0] = C ? E[0] : 1'bz;  // Controlled_Buffer controlled_buffer_3
  assign S[1] = C ? E[1] : 1'bz;  // Controlled_Buffer controlled_buffer_4
endmodule
